# Fritzing sketch doorsensor (saved by Fritzing 0.9.3b)
breadboards: 1

parts:
  Q1 = PNP-Transistor [package="TO92 [THT]"]
  U1 = ESP8266 WiFi Module [part_number=ESP8266]
  R1 = Resistor [tolerance=±5% resistance=1k package=THT]
  R4 = Resistor [tolerance=±5% resistance=1k package=THT]
  R5 = Resistor [tolerance=±5% resistance=10k package=THT]
  S1 = SWITCH-MOMENTARY-2 [package=reed_switch_plastic]
  R6 = Resistor [tolerance=±5% resistance=10k package=THT]
  V1 = DC Power [voltage=3.3V]

nets:
  N1: Q1.E, U1.VCC, S1.2, V1.V+
  N2: Q1.B, R5.Pin_0, S1.1
  N3: Q1.C, R1.Pin_1, R4.Pin_1, R6.Pin_1
  N4: U1.GPIO_0, R1.Pin_0
  N5: U1.CH_PD, R4.Pin_0
  N6: U1.GND, R5.Pin_1, R6.Pin_0, V1.V-

custom parts:
  ESP8266 WiFi Module: Generic WiFi Module based on the ESP8266 with onboard PCB antenna and UART communications
